# Fritzing sketch PiGO2_schema_1 (saved by Fritzing 0.9.3b)
breadboards: 1

parts:
  MCU1 = Raspberry Pi Zero
  IC2 = H-Bridge [package=THT]
  IC3 = H-Bridge [package=THT]
  BatteryBox = Battery block 9V
  PiconZero = IC, DIP package, 38 pins [chip_label=PiconZero]
  M1 = DC Motor
  M2 = DC Motor
  M3 = DC Motor
  M4 = DC Motor
  M5 = DC Motor
  Powerbank = DC Power [voltage=5V]

nets:
  N1: MCU1.pin_3, PiconZero.pin1
  N2: MCU1.pin_4, Powerbank.V+
  N3: MCU1.pin_5, PiconZero.pin2
  N4: MCU1.pin_6, Powerbank.V-
  N5: IC2.1A, PiconZero.pin38
  N6: IC2.1Y, M3.pin_2
  GND1: IC2.GND1, IC2.GND2, IC2.GND3, IC2.GND4, IC3.GND1, IC3.GND2, IC3.GND3, IC3.GND4, BatteryBox.-, PiconZero.pin20
  N7: IC2.2Y, M3.pin_1
  N8: IC2.2A, PiconZero.pin37
  N9: IC2.VCC2, IC2.VCC1, IC3.VCC2, IC3.VCC1, BatteryBox.+, PiconZero.pin19
  N10: IC2.3A, PiconZero.pin35
  N11: IC2.3Y, M4.pin_1
  N12: IC2.4Y, M4.pin_2
  N13: IC2.4A, PiconZero.pin36
  N14: IC3.3A, PiconZero.pin33
  N15: IC3.3Y, M5.pin_1
  N16: IC3.4Y, M5.pin_2
  N17: IC3.4A, PiconZero.pin34
  N18: PiconZero.pin3, M1.pin_1
  N19: PiconZero.pin4, M1.pin_2
  N20: PiconZero.pin5, M2.pin_1
  N21: PiconZero.pin6, M2.pin_2
